# Fritzing sketch FilamentFuserController (saved by Fritzing 0.9.3b)

parts:
  Fan = female pin header, 2 pins [form="♀ (female)"]
  Temp_Sensor = female pin header, 2 pins [form="♀ (female)"]
  Power = Power plug
  Q1 = MOSFET-NCHANNEL [part_number="IRLZ 34N" package=to220v]
  R3 = Resistor [tolerance=±5% resistance=100k package=THT]
  R1 = Resistor [tolerance=±5% resistance=100k package=THT]
  Bauteil1 = Arduino Prototyping Shield
  Heater = female pin header, 2 pins [form="♀ (female)"]
  MP1584EN_Board_5V = MP1584EN Power Regulator Board [part_number=MP1584EN]
  J1 = female pin header, 2 pins [form="♀ (female)"]
  R2 = Resistor [tolerance=±5% resistance=10 package=THT]
  R4 = Resistor [tolerance=±1% resistance=680 package=THT]
  LED1 = LED - 5mm [color="Red (633nm)" package="5 mm [THT]"]

nets:
  N1: Fan.pin1, Power.VCC, Bauteil1.N$67, Bauteil1.N$74, Bauteil1.N$118, Bauteil1.N$237, Bauteil1.N$239, MP1584EN_Board_5V.IN_+
  GND: Fan.pin2, Temp_Sensor.pin2, Power.GND, Q1.S, R3.Pin_0, Bauteil1.GND, Bauteil1.N$41, Bauteil1.N$42, Bauteil1.N$75, Bauteil1.N$87, Bauteil1.N$201, Bauteil1.N$353, Bauteil1.N$416, Bauteil1.N$423, Bauteil1.N$428, Bauteil1.N$429, MP1584EN_Board_5V.IN_-, MP1584EN_Board_5V.OUT_-
  N2: Temp_Sensor.pin1, R1.Pin_1, Bauteil1.A0, Bauteil1.N$27, Bauteil1.N$28, Bauteil1.N$33, Bauteil1.N$34, Bauteil1.N$335
  N3: Q1.G, Bauteil1.N$368
  N4: Q1.D, Bauteil1.N$65, Bauteil1.N$66, Bauteil1.N$326, Heater.pin2
  N5: R3.Pin_1, Bauteil1.D7, Bauteil1.N$82, Bauteil1.N$377, R2.Pin_1
  N6: R1.Pin_0, Bauteil1.+5V, Bauteil1.N$50, J1.pin1
  N7: Bauteil1.N$39, Bauteil1.N$51, MP1584EN_Board_5V.OUT_+, J1.pin2
  N8: Bauteil1.N$72, R4.Pin_0
  N9: Bauteil1.N$76, Bauteil1.N$78, Bauteil1.N$79, Heater.pin1
  N10: Bauteil1.N$274, R4.Pin_1, LED1.anode
  N11: Bauteil1.N$278, Bauteil1.N$292, LED1.cathode
  N12: Bauteil1.N$323, R2.Pin_0

custom parts:
  MP1584EN Power Regulator Board: The MP1584EN is a high frequency step-down switching regulator. The input voltage range is 4.5V to 28V. The output voltage is set by the board's potentiometer.
